# Fritzing sketch Schematic (saved by Fritzing 0.9.2b)
circuit board: 4.35876cm x 3.79432cm
breadboards: 1

parts:
  neopixel4 = Neopixel Ring 12
  C1 = Ceramic Capacitor [capacitance=1mF package="100 mil [THT, multilayer]"]
  neopixel3 = Neopixel Ring 12  # not connected
  Part2 = Adafruit AT42QT1010 Standalone Momentary Capacitive Touch Sensor [part_number="Adafruit #1374"]
  R1 = Resistor [tolerance=±5% resistance=220 package=THT]
  Part1 = Photon

nets:
  VCC: neopixel4.VCC, C1.1, Part1.VIN
  GND: C1.0, Part2.GND, Part1.GND
  VDD: Part2.VDD, Part1.3V3
  N1: Part2.OUT, Part1.D2
  N2: R1.Pin_1, Part1.D3

custom parts:
  Neopixel Ring 12: Neopixel Ring x12
  Adafruit AT42QT1010 Standalone Momentary Capacitive Touch Sensor: This breakout board is the simplest way to create a project with a single "momentary" capacitive touch sensor. No microcontroller is required here - just power with 1.8 to 5.5VDC and touch the pad to activate the sensor. When a capacitive load is detected (e.g. a person touches the sensor-pad area) the red LED lights up and the output pin goes high. You can also solder a wire to the middle pad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
