# Fritzing sketch Schematic (saved by Fritzing 0.9.2b)
breadboards: 1

parts:
  Part1 = Photon
  S1 = Momentary Switch [package=ksa_sealed_tac_switch]
  neopixel3 = Neopixel Ring 12
  neopixel4 = Neopixel Ring 12
  C1 = Ceramic Capacitor [capacitance=100nF package="100 mil [THT, multilayer]"]
  R1 = Resistor [tolerance=±5% resistance=220 package="0402 [SMD]"]
  R2 = Resistor [tolerance=±5% resistance=220 package="0402 [SMD]"]

nets:
  GND: Part1.GND, S1.3, neopixel3.GND, neopixel4.GND, C1.0
  VCC: Part1.VIN, neopixel3.VCC, neopixel4.VCC, C1.1
  N1: Part1.D2, R1.Pin_1
  N2: Part1.D3, S1.1, R2.Pin_0
  N3: Part1.3V3, R2.Pin_1
  N4: neopixel3.IN, neopixel4.IN, R1.Pin_0

custom parts:
  Neopixel Ring 12: Neopixel Ring x12
